// Logisim project f2f1f0.circ as structural Verilog: 1 circuit, main circuit main
module main (
  input  A,
  input  B,
  input  C,
  input  D,
  output F2,
  output F1,
  output F0
);

  wire and_1_out, and_2_out, and_3_out, and_4_out, and_5_out, and_6_out, and_7_out, not_1_out, not_2_out,
       not_3_out, not_4_out, not_5_out, not_6_out;

  not not_1 (not_1_out, A);
  not not_2 (not_2_out, C);
  not not_3 (not_3_out, B);
  not not_4 (not_4_out, D);
  not not_5 (not_5_out, B);
  not not_6 (not_6_out, D);
  and and_1 (and_1_out, A, C);
  and and_2 (and_2_out, A, B, D);
  and and_3 (and_3_out, C, B, D);
  and and_4 (and_4_out, A, B, C, D);
  and and_5 (and_5_out, not_1_out, B, not_2_out, D);
  and and_6 (and_6_out, not_5_out, D);
  and and_7 (and_7_out, B, not_6_out);
  or or_1 (F0, and_6_out, and_7_out);
  or or_2 (F2, and_1_out, and_2_out, and_3_out);
  or or_3 (F1, and_4_out, and_5_out, not_3_out, not_4_out);
endmodule
