// Logisim project 8 битный сумматор.circ as structural Verilog: 3 circuits, main circuit Полусуматор
module \Полусуматор  (
  input  A,
  input  B,
  output \Сумма ,
  output \Перевод 
);

  xor xor_1 (\Сумма , A, B);
  and and_1 (\Перевод , B, A);
endmodule

module \_1_битный_сумматор  (
  input  \Ввод_из_перевода ,
  input  \А ,
  input  \В ,
  output \Сумма ,
  output \Перевод 
);

  wire \полусуматор_1_перевод , \полусуматор_1_сумма , \полусуматор_2_перевод ;

  \Полусуматор  \u_полусуматор_1  (
    .A(\А ), .B(\В ), .\Сумма (\полусуматор_1_сумма ), .\Перевод (\полусуматор_1_перевод ));
  \Полусуматор  \u_полусуматор_2  (
    .A(\Ввод_из_перевода ), .B(\полусуматор_1_сумма ), .\Сумма (\Сумма ), .\Перевод (\полусуматор_2_перевод ));
  or or_1 (\Перевод , \полусуматор_2_перевод , \полусуматор_1_перевод );
endmodule

module \_8_битный_сумматор  (
  input  [7:0] \В ,
  input  [7:0] \А ,
  output [8:0] out_3
);

  wire \n1_битный_сумматор_1_перевод , \n1_битный_сумматор_2_перевод , \n1_битный_сумматор_3_перевод ,
       \n1_битный_сумматор_4_перевод , \n1_битный_сумматор_5_перевод , \n1_битный_сумматор_6_перевод ,
       \n1_битный_сумматор_7_перевод ;

  // Probe on \В 
  // Probe on \А 
  \_1_битный_сумматор  \u_1_битный_сумматор_1  (
    .\А (\А [0]), .\В (\В [0]), .\Ввод_из_перевода (1'b0), .\Сумма (out_3[0]),
    .\Перевод (\n1_битный_сумматор_1_перевод ));
  \_1_битный_сумматор  \u_1_битный_сумматор_2  (
    .\А (\А [1]), .\В (\В [1]), .\Ввод_из_перевода (\n1_битный_сумматор_1_перевод ), .\Сумма (out_3[1]),
    .\Перевод (\n1_битный_сумматор_2_перевод ));
  \_1_битный_сумматор  \u_1_битный_сумматор_3  (
    .\А (\А [2]), .\В (\В [2]), .\Ввод_из_перевода (\n1_битный_сумматор_2_перевод ), .\Сумма (out_3[2]),
    .\Перевод (\n1_битный_сумматор_3_перевод ));
  \_1_битный_сумматор  \u_1_битный_сумматор_4  (
    .\А (\А [3]), .\В (\В [3]), .\Ввод_из_перевода (\n1_битный_сумматор_3_перевод ), .\Сумма (out_3[3]),
    .\Перевод (\n1_битный_сумматор_4_перевод ));
  \_1_битный_сумматор  \u_1_битный_сумматор_5  (
    .\А (\А [4]), .\В (\В [4]), .\Ввод_из_перевода (\n1_битный_сумматор_4_перевод ), .\Сумма (out_3[4]),
    .\Перевод (\n1_битный_сумматор_5_перевод ));
  \_1_битный_сумматор  \u_1_битный_сумматор_6  (
    .\А (\А [5]), .\В (\В [5]), .\Ввод_из_перевода (\n1_битный_сумматор_5_перевод ), .\Сумма (out_3[5]),
    .\Перевод (\n1_битный_сумматор_6_перевод ));
  \_1_битный_сумматор  \u_1_битный_сумматор_7  (
    .\А (\А [6]), .\В (\В [6]), .\Ввод_из_перевода (\n1_битный_сумматор_6_перевод ), .\Сумма (out_3[6]),
    .\Перевод (\n1_битный_сумматор_7_перевод ));
  \_1_битный_сумматор  \u_1_битный_сумматор_8  (
    .\А (\А [7]), .\В (\В [7]), .\Ввод_из_перевода (\n1_битный_сумматор_7_перевод ), .\Сумма (out_3[7]),
    .\Перевод (out_3[8]));
  // Probe on out_3
endmodule
