// Logisim project 8-бит сумматор и вычислитель.circ as structural Verilog: 5 circuits, main circuit Полусуматор
module \Полусуматор  (
  input  A,
  input  B,
  output \Сумма ,
  output \Перевод 
);

  xor xor_1 (\Сумма , A, B);
  and and_1 (\Перевод , B, A);
endmodule

module \_1_битный_сумматор  (
  input  \Ввод_из_перевода ,
  input  \А ,
  input  \В ,
  output \Сумма ,
  output \Перевод 
);

  wire \полусуматор_1_перевод , \полусуматор_1_сумма , \полусуматор_2_перевод ;

  \Полусуматор  \u_полусуматор_1  (
    .A(\А ), .B(\В ), .\Сумма (\полусуматор_1_сумма ), .\Перевод (\полусуматор_1_перевод ));
  \Полусуматор  \u_полусуматор_2  (
    .A(\Ввод_из_перевода ), .B(\полусуматор_1_сумма ), .\Сумма (\Сумма ), .\Перевод (\полусуматор_2_перевод ));
  or or_1 (\Перевод , \полусуматор_2_перевод , \полусуматор_1_перевод );
endmodule

module \_8_битный_сумматор  (
  input  in_1,
  input  [7:0] \В ,
  input  [7:0] \А ,
  output [7:0] out_4,
  output \Переполнение 
);

  wire \n1_битный_сумматор_1_перевод , \n1_битный_сумматор_2_перевод , \n1_битный_сумматор_3_перевод ,
       \n1_битный_сумматор_4_перевод , \n1_битный_сумматор_5_перевод , \n1_битный_сумматор_6_перевод ,
       \n1_битный_сумматор_7_перевод ;

  // Probe on \В 
  // Probe on \А 
  \_1_битный_сумматор  \u_1_битный_сумматор_1  (
    .\А (\А [0]), .\В (\В [0]), .\Ввод_из_перевода (in_1), .\Сумма (out_4[0]),
    .\Перевод (\n1_битный_сумматор_1_перевод ));
  \_1_битный_сумматор  \u_1_битный_сумматор_2  (
    .\А (\А [1]), .\В (\В [1]), .\Ввод_из_перевода (\n1_битный_сумматор_1_перевод ), .\Сумма (out_4[1]),
    .\Перевод (\n1_битный_сумматор_2_перевод ));
  \_1_битный_сумматор  \u_1_битный_сумматор_3  (
    .\А (\А [2]), .\В (\В [2]), .\Ввод_из_перевода (\n1_битный_сумматор_2_перевод ), .\Сумма (out_4[2]),
    .\Перевод (\n1_битный_сумматор_3_перевод ));
  \_1_битный_сумматор  \u_1_битный_сумматор_4  (
    .\А (\А [3]), .\В (\В [3]), .\Ввод_из_перевода (\n1_битный_сумматор_3_перевод ), .\Сумма (out_4[3]),
    .\Перевод (\n1_битный_сумматор_4_перевод ));
  \_1_битный_сумматор  \u_1_битный_сумматор_5  (
    .\А (\А [4]), .\В (\В [4]), .\Ввод_из_перевода (\n1_битный_сумматор_4_перевод ), .\Сумма (out_4[4]),
    .\Перевод (\n1_битный_сумматор_5_перевод ));
  \_1_битный_сумматор  \u_1_битный_сумматор_6  (
    .\А (\А [5]), .\В (\В [5]), .\Ввод_из_перевода (\n1_битный_сумматор_5_перевод ), .\Сумма (out_4[5]),
    .\Перевод (\n1_битный_сумматор_6_перевод ));
  \_1_битный_сумматор  \u_1_битный_сумматор_7  (
    .\А (\А [6]), .\В (\В [6]), .\Ввод_из_перевода (\n1_битный_сумматор_6_перевод ), .\Сумма (out_4[6]),
    .\Перевод (\n1_битный_сумматор_7_перевод ));
  \_1_битный_сумматор  \u_1_битный_сумматор_8  (
    .\А (\А [7]), .\В (\В [7]), .\Ввод_из_перевода (\n1_битный_сумматор_7_перевод ), .\Сумма (out_4[7]),
    .\Перевод (\Переполнение ));
  // Probe on out_4
endmodule

module \Инвертор  (
  input  in_1,
  input  [7:0] in_2,
  output [7:0] out_3
);

  // Probe on in_2
  xor xor_1 (out_3[0], in_2[0], in_1);
  xor xor_2 (out_3[1], in_2[1], in_1);
  xor xor_3 (out_3[2], in_2[2], in_1);
  xor xor_4 (out_3[3], in_2[3], in_1);
  xor xor_5 (out_3[4], in_2[4], in_1);
  xor xor_6 (out_3[5], in_2[5], in_1);
  xor xor_7 (out_3[6], in_2[6], in_1);
  xor xor_8 (out_3[7], in_2[7], in_1);
  // Probe on out_3
endmodule

module \Вычислитель  (
  input  [7:0] \В ,
  input  in_2,
  input  [7:0] \А ,
  output [7:0] out_4,
  output out_5
);

  wire [7:0] \инвертор_1_out_3 ;

  // Probe on \В 
  // Probe on \В 
  // Probe on \А 
  // Probe on \А 
  \Инвертор  \u_инвертор_1  (.in_2(\В ), .out_3(\инвертор_1_out_3 ), .in_1(in_2));
  // Probe on \инвертор_1_out_3 
  // Probe on out_4
  // Probe on out_4
  \_8_битный_сумматор  \u_8_битный_сумматор_1  (
    .\В (\инвертор_1_out_3 ), .\А (\А ), .out_4(out_4), .\Переполнение (out_5), .in_1(1'b1));
endmodule
