// Logisim project LR_1.circ as structural Verilog: 9 circuits, main circuit RS-триггер
module \RS_триггер  (
  input  \Сброс ,
  input  \Установка ,
  output out_3,
  output out_4
);

  nor nor_1 (out_3, \Сброс , out_4);
  nor nor_2 (out_4, out_3, \Установка );
endmodule

module \D_триггер  (
  input  \Сброс ,
  input  \Блок ,
  input  \Данные ,
  output out_4,
  output out_5
);

  wire and_1_out, and_2_out, not_1_out, or_1_out;

  not not_1 (not_1_out, \Данные );
  and and_1 (and_1_out, not_1_out, \Блок );
  and and_2 (and_2_out, \Блок , \Данные );
  or or_1 (or_1_out, \Сброс , and_1_out);
  \RS_триггер  \rs_триггер_1  (.\Сброс (or_1_out), .\Установка (and_2_out), .out_3(out_4), .out_4(out_5));
endmodule

module \D_триггер__нижнего_уровня  (
  input  in_1,
  input  in_2,
  input  in_3,
  output out_4
);

  wire not_1_out;

  not not_1 (not_1_out, in_2);
  \D_триггер  \d_триггер_1  (.\Блок (not_1_out), .\Данные (in_3), .\Сброс (in_1), .out_4(out_4));  // open: out_5
endmodule

module \D_триггер__передний_фронд  (
  input  \Сброс ,
  input  \Блок ,
  input  \Данные ,
  output out_4
);

  wire not_1_out, or_1_out, or_2_out, or_3_out;

  not not_1 (not_1_out, \Данные );
  or or_1 (or_1_out, not_1_out, \Блок );
  or or_2 (or_2_out, \Блок , \Данные );
  or or_3 (or_3_out, \Сброс , or_1_out);
  \RS_триггер  \rs_триггер_1  (.\Сброс (or_3_out), .\Установка (or_2_out), .out_3(out_4));  // open: out_4
endmodule

module \D_триггер__нижний_фронд  (
  input  \Сброс ,
  input  \Блок ,
  input  \Данные ,
  output out_4
);

  wire not_1_out, not_2_out, or_1_out, or_2_out, or_3_out;

  not not_1 (not_1_out, \Блок );
  not not_2 (not_2_out, \Данные );
  or or_1 (or_1_out, not_2_out, not_1_out);
  or or_2 (or_2_out, not_1_out, \Данные );
  or or_3 (or_3_out, \Сброс , or_1_out);
  \RS_триггер  \rs_триггер_1  (.\Сброс (or_3_out), .\Установка (or_2_out), .out_3(out_4));  // open: out_4
endmodule

module \JK_триггер_из_RS  (
  input  \Сброс__K ,
  input  \Блок ,
  input  \Установить__J ,
  output out_4,
  output out_5
);

  wire and_1_out, and_2_out, or_1_out, or_2_out;

  or or_1 (or_1_out, out_5, \Сброс__K );
  or or_2 (or_2_out, \Установить__J , out_4);
  and and_1 (and_1_out, or_1_out, \Блок );
  and and_2 (and_2_out, \Блок , or_2_out);
  \RS_триггер  \rs_триггер_1  (.\Сброс (and_1_out), .\Установка (and_2_out), .out_3(out_4), .out_4(out_5));
endmodule

module \JK_триггер_из_D  (
  input  \Сброс__K ,
  input  \Блок ,
  input  \Установить__J ,
  output out_4,
  output out_5
);

  wire or_1_out, or_2_out;

  or or_1 (or_1_out, out_5, \Сброс__K );
  or or_2 (or_2_out, \Установить__J , out_4);
  \D_триггер  \d_триггер_1  (.\Блок (\Блок ), .\Данные (or_2_out), .\Сброс (or_1_out), .out_4(out_4), .out_5(out_5));
endmodule

module \TC_триггер_из_RS  (
  input  \Блок__C ,
  input  \Установить__T ,
  output out_3,
  output out_4
);

  wire and_1_out, and_2_out, not_1_out, or_1_out, or_2_out;

  not not_1 (not_1_out, \Установить__T );
  or or_1 (or_1_out, out_4, not_1_out);
  or or_2 (or_2_out, \Установить__T , out_3);
  and and_1 (and_1_out, or_1_out, \Блок__C );
  and and_2 (and_2_out, \Блок__C , or_2_out);
  \RS_триггер  \rs_триггер_1  (.\Сброс (and_1_out), .\Установка (and_2_out), .out_3(out_3), .out_4(out_4));
endmodule

module \TC_триггер_из_D  (
  input  \Блок__C ,
  input  \Установить__T ,
  output out_3,
  output out_4
);

  wire not_1_out, or_1_out, or_2_out;

  not not_1 (not_1_out, \Установить__T );
  or or_1 (or_1_out, out_4, not_1_out);
  or or_2 (or_2_out, \Установить__T , out_3);
  \D_триггер  \d_триггер_1  (.\Блок (\Блок__C ), .\Данные (or_2_out), .\Сброс (or_1_out), .out_4(out_3), .out_5(out_4));
endmodule
