// Logisim project LR_2.circ as structural Verilog: 14 circuits, main circuit Счетчик
module main (
  input  [7:0] in_1,
  input  in_2,
  input  [2:0] in_3,
  output [7:0] out_4
);

  wire clock_1_out, demultiplexer_1_out0, demultiplexer_1_out1, demultiplexer_1_out2, demultiplexer_1_out3,
       demultiplexer_1_out4, demultiplexer_1_out5, demultiplexer_1_out6, demultiplexer_1_out7;
  wire [7:0] register_1_q, register_2_q, register_3_q, register_4_q, register_5_q, register_6_q,
       register_7_q, register_8_q;

  Demultiplexer #(.select(3)) demultiplexer_1 (
    .out0(demultiplexer_1_out0), .out1(demultiplexer_1_out1), .out2(demultiplexer_1_out2),
    .out3(demultiplexer_1_out3), .out4(demultiplexer_1_out4), .out5(demultiplexer_1_out5),
    .out6(demultiplexer_1_out6), .out7(demultiplexer_1_out7), .in(in_2), .sel(in_3));  // open: en
  Clock clock_1 (.out(clock_1_out));
  Register register_1 (.D(in_1), .en(demultiplexer_1_out0), .Q(register_1_q), .clk(clock_1_out));  // open: clr
  Register register_2 (.D(in_1), .en(demultiplexer_1_out1), .Q(register_2_q), .clk(clock_1_out));  // open: clr
  Register register_3 (.D(in_1), .en(demultiplexer_1_out2), .Q(register_3_q), .clk(clock_1_out));  // open: clr
  Register register_4 (.D(in_1), .en(demultiplexer_1_out3), .Q(register_4_q));  // open: clk, clr
  Register register_5 (.D(in_1), .en(demultiplexer_1_out4), .Q(register_5_q), .clk(clock_1_out));  // open: clr
  Register register_6 (.D(in_1), .en(demultiplexer_1_out5), .Q(register_6_q), .clk(clock_1_out));  // open: clr
  Register register_7 (.D(in_1), .en(demultiplexer_1_out6), .Q(register_7_q), .clk(clock_1_out));  // open: clr
  Register register_8 (.D(in_1), .en(demultiplexer_1_out7), .Q(register_8_q), .clk(clock_1_out));  // open: clr
  Multiplexer #(.select(3), .width(8)) multiplexer_1 (
    .in0(register_1_q), .in1(register_2_q), .in2(register_3_q), .in3(register_4_q), .in4(register_5_q),
    .in5(register_6_q), .in6(register_7_q), .in7(register_8_q), .out(out_4), .sel(in_3));  // open: en
endmodule

module \Счетчик  (
  input  [3:0] in_1,
  input  \выч_уст ,
  input  \сброс ,
  input  \запись ,
  input  in_5,
  input  [3:0] in_6,
  input  in_7,
  input  in_8,
  output [3:0] out_9,
  output [3:0] out_10
);

  wire and_1_out, and_2_out, and_4_out, and_5_out, and_6_out, and_7_out, and_8_out, and_9_out, clock_1_out,
       clock_2_out, d_ff_1_qn, d_ff_2_qn, d_ff_3_qn, d_ff_4_qn, not_1_out, or_2_out, or_3_out, or_4_out;

  // Probe on in_1
  // OR_Gate or_1 is placed but not wired
  not not_1 (not_1_out, \запись );
  Clock clock_1 (.out(clock_1_out));
  and and_1 (and_1_out, \выч_уст , not_1_out, clock_1_out);
  and and_2 (and_2_out, and_1_out, in_1[0]);
  // AND_Gate and_3 is placed but not wired
  D_Flip_Flop d_ff_1 (
    .clk(clock_1_out), .D(d_ff_1_qn), .Q(out_9[0]), .Qn(d_ff_1_qn), .preset(and_2_out), .en(\запись ),
    .reset(\сброс ));
  and and_4 (and_4_out, \выч_уст , out_9[0]);
  // Probe on out_9[0]
  Clock clock_2 (.out(clock_2_out));
  and and_5 (and_5_out, and_1_out, in_1[1]);
  or or_2 (or_2_out, and_4_out, d_ff_1_qn);
  Counter #(.width(4), .max('hf)) counter_1 (
    .load(in_5), .D(in_6), .count(in_7), .Q(out_10), .clk(clock_2_out), .clr(in_8));  // open: carry
  and and_6 (and_6_out, \выч_уст , out_9[1]);
  // Probe on out_9[1]
  D_Flip_Flop d_ff_2 (
    .clk(or_2_out), .D(d_ff_2_qn), .Q(out_9[1]), .Qn(d_ff_2_qn), .preset(and_5_out), .en(\запись ),
    .reset(\сброс ));
  and and_7 (and_7_out, and_1_out, in_1[2]);
  or or_3 (or_3_out, and_6_out, d_ff_2_qn);
  D_Flip_Flop d_ff_3 (
    .clk(or_3_out), .D(d_ff_3_qn), .Q(out_9[2]), .Qn(d_ff_3_qn), .preset(and_7_out), .en(\запись ),
    .reset(\сброс ));
  and and_8 (and_8_out, \выч_уст , out_9[2]);
  // Probe on out_9[2]
  and and_9 (and_9_out, and_1_out, in_1[3]);
  or or_4 (or_4_out, and_8_out, d_ff_3_qn);
  // Probe on out_9[3]
  D_Flip_Flop d_ff_4 (
    .clk(or_4_out), .D(d_ff_4_qn), .Q(out_9[3]), .Qn(d_ff_4_qn), .preset(and_9_out), .en(\запись ),
    .reset(\сброс ));
  // Probe on out_9
endmodule

module \_8_битный_регистр__синхронный  (
  input  [7:0] in_1,
  input  \Запись ,
  input  \Очистка ,
  output [7:0] out_4
);

  wire clock_1_out;

  Clock clock_1 (.out(clock_1_out));
  D_Flip_Flop d_ff_1 (
    .clk(clock_1_out), .D(in_1[0]), .Q(out_4[0]), .en(\Запись ), .reset(\Очистка ));  // open: Qn, preset
  D_Flip_Flop d_ff_2 (
    .clk(clock_1_out), .D(in_1[1]), .Q(out_4[1]), .en(\Запись ), .reset(\Очистка ));  // open: Qn, preset
  D_Flip_Flop d_ff_3 (
    .clk(clock_1_out), .D(in_1[2]), .Q(out_4[2]), .en(\Запись ), .reset(\Очистка ));  // open: Qn, preset
  D_Flip_Flop d_ff_4 (
    .clk(clock_1_out), .D(in_1[3]), .Q(out_4[3]), .en(\Запись ), .reset(\Очистка ));  // open: Qn, preset
  D_Flip_Flop d_ff_5 (
    .clk(clock_1_out), .D(in_1[4]), .Q(out_4[4]), .en(\Запись ), .reset(\Очистка ));  // open: Qn, preset
  D_Flip_Flop d_ff_6 (
    .clk(clock_1_out), .D(in_1[5]), .Q(out_4[5]), .en(\Запись ), .reset(\Очистка ));  // open: Qn, preset
  D_Flip_Flop d_ff_7 (
    .clk(clock_1_out), .D(in_1[6]), .Q(out_4[6]), .en(\Запись ), .reset(\Очистка ));  // open: Qn, preset
  D_Flip_Flop d_ff_8 (
    .clk(clock_1_out), .D(in_1[7]), .Q(out_4[7]), .en(\Запись ), .reset(\Очистка ));  // open: Qn, preset
endmodule

module \_8_битный_регистр__ассинхронный  (
  input  \Запись ,
  input  [7:0] in_2,
  input  \Очистка ,
  output [7:0] out_4
);

  D_Flip_Flop d_ff_1 (.clk(\Запись ), .D(in_2[0]), .Q(out_4[0]), .reset(\Очистка ));  // open: Qn, preset, en
  D_Flip_Flop d_ff_2 (.clk(\Запись ), .D(in_2[1]), .Q(out_4[1]), .reset(\Очистка ));  // open: Qn, preset, en
  D_Flip_Flop d_ff_3 (.clk(\Запись ), .D(in_2[2]), .Q(out_4[2]), .reset(\Очистка ));  // open: Qn, preset, en
  D_Flip_Flop d_ff_4 (.clk(\Запись ), .D(in_2[3]), .Q(out_4[3]), .reset(\Очистка ));  // open: Qn, preset, en
  D_Flip_Flop d_ff_5 (.clk(\Запись ), .D(in_2[4]), .Q(out_4[4]), .reset(\Очистка ));  // open: Qn, preset, en
  D_Flip_Flop d_ff_6 (.clk(\Запись ), .D(in_2[5]), .Q(out_4[5]), .reset(\Очистка ));  // open: Qn, preset, en
  D_Flip_Flop d_ff_7 (.clk(\Запись ), .D(in_2[6]), .Q(out_4[6]), .reset(\Очистка ));  // open: Qn, preset, en
  D_Flip_Flop d_ff_8 (.clk(\Запись ), .D(in_2[7]), .Q(out_4[7]), .reset(\Очистка ));  // open: Qn, preset, en
endmodule

module \_1_битный_сумматор  (
  input  \Ввод_из_перевода ,
  input  A,
  input  B,
  output \Сумма ,
  output \Перевод 
);

  wire and_1_out, and_2_out, xor_1_out;

  xor xor_1 (xor_1_out, A, B);
  and and_1 (and_1_out, B, A);
  xor xor_2 (\Сумма , \Ввод_из_перевода , xor_1_out);
  and and_2 (and_2_out, xor_1_out, \Ввод_из_перевода );
  or or_1 (\Перевод , and_2_out, and_1_out);
endmodule

module \_8_битный_сумматор  (
  input  in_1,
  input  [7:0] \В ,
  input  [7:0] \А ,
  output [7:0] out_4,
  output \Переполнение 
);

  wire \n1_битный_сумматор_1_перевод , \n1_битный_сумматор_2_перевод , \n1_битный_сумматор_3_перевод ,
       \n1_битный_сумматор_4_перевод , \n1_битный_сумматор_5_перевод , \n1_битный_сумматор_6_перевод ,
       \n1_битный_сумматор_7_перевод ;

  // Probe on \В 
  // Probe on \А 
  \_1_битный_сумматор  \u_1_битный_сумматор_1  (
    .\Ввод_из_перевода (in_1), .A(\А [0]), .B(\В [0]), .\Сумма (out_4[0]),
    .\Перевод (\n1_битный_сумматор_1_перевод ));
  \_1_битный_сумматор  \u_1_битный_сумматор_2  (
    .\Ввод_из_перевода (\n1_битный_сумматор_1_перевод ), .A(\А [1]), .B(\В [1]), .\Сумма (out_4[1]),
    .\Перевод (\n1_битный_сумматор_2_перевод ));
  \_1_битный_сумматор  \u_1_битный_сумматор_3  (
    .\Ввод_из_перевода (\n1_битный_сумматор_2_перевод ), .A(\А [2]), .B(\В [2]), .\Сумма (out_4[2]),
    .\Перевод (\n1_битный_сумматор_3_перевод ));
  \_1_битный_сумматор  \u_1_битный_сумматор_4  (
    .\Ввод_из_перевода (\n1_битный_сумматор_3_перевод ), .A(\А [3]), .B(\В [3]), .\Сумма (out_4[3]),
    .\Перевод (\n1_битный_сумматор_4_перевод ));
  \_1_битный_сумматор  \u_1_битный_сумматор_5  (
    .\Ввод_из_перевода (\n1_битный_сумматор_4_перевод ), .A(\А [4]), .B(\В [4]), .\Сумма (out_4[4]),
    .\Перевод (\n1_битный_сумматор_5_перевод ));
  \_1_битный_сумматор  \u_1_битный_сумматор_6  (
    .\Ввод_из_перевода (\n1_битный_сумматор_5_перевод ), .A(\А [5]), .B(\В [5]), .\Сумма (out_4[5]),
    .\Перевод (\n1_битный_сумматор_6_перевод ));
  \_1_битный_сумматор  \u_1_битный_сумматор_7  (
    .\Ввод_из_перевода (\n1_битный_сумматор_6_перевод ), .A(\А [6]), .B(\В [6]), .\Сумма (out_4[6]),
    .\Перевод (\n1_битный_сумматор_7_перевод ));
  \_1_битный_сумматор  \u_1_битный_сумматор_8  (
    .\Ввод_из_перевода (\n1_битный_сумматор_7_перевод ), .A(\А [7]), .B(\В [7]), .\Сумма (out_4[7]),
    .\Перевод (\Переполнение ));
  // Probe on out_4
endmodule

module \Инвертер  (
  input  in_1,
  input  [7:0] in_2,
  output [7:0] out_3
);

  // Probe on in_2
  xor xor_1 (out_3[0], in_2[0], in_1);
  xor xor_2 (out_3[1], in_2[1], in_1);
  xor xor_3 (out_3[2], in_2[2], in_1);
  xor xor_4 (out_3[3], in_2[3], in_1);
  xor xor_5 (out_3[4], in_2[4], in_1);
  xor xor_6 (out_3[5], in_2[5], in_1);
  xor xor_7 (out_3[6], in_2[6], in_1);
  xor xor_8 (out_3[7], in_2[7], in_1);
  // Probe on out_3
endmodule

module \Сумматор_Вычислитель_с_памятью  (
  input  in_1,
  input  [7:0] in_2,
  input  in_3,
  input  in_4,
  input  [7:0] in_5,
  output [7:0] out_6,
  output out_7
);

  wire [7:0] \n8_битный_сумматор_1_out_4 , or_1_out, \инвертер_1_out_3 ;

  // Probe on in_2
  // Probe on in_5
  \Инвертер  \u_инвертер_1  (.in_2(in_5), .out_3(\инвертер_1_out_3 ), .in_1(in_4));
  // Probe on \n8_битный_сумматор_1_out_4 
  \_8_битный_сумматор  \u_8_битный_сумматор_1  (
    .in_1(1'b0), .\В (\инвертер_1_out_3 ), .\А (out_6), .out_4(\n8_битный_сумматор_1_out_4 ),
    .\Переполнение (out_7));
  // Probe on or_1_out
  assign or_1_out = in_2 | \n8_битный_сумматор_1_out_4 ;  // OR_Gate or_1, 8 bits wide
  \_8_битный_регистр__ассинхронный  \u_8_битный_регистр_ассинхронный_1  (
    .in_2(or_1_out), .out_4(out_6), .\Запись (in_1), .\Очистка (in_3));
  // Probe on out_6

  // Notes on the sheet:
  //   А
  //   В
endmodule

module \_32_8ram__тестовая_версия  (
  input  [7:0] in_1,
  input  in_2,
  input  [4:0] in_3,
  output [7:0] out_4
);

  wire demultiplexer_1_out0, demultiplexer_1_out1, demultiplexer_1_out2, demultiplexer_1_out3,
       demultiplexer_1_out4, demultiplexer_1_out5, demultiplexer_1_out6, demultiplexer_1_out7,
       demultiplexer_1_out8, demultiplexer_1_out9, demultiplexer_1_out10, demultiplexer_1_out11,
       demultiplexer_1_out12, demultiplexer_1_out13, demultiplexer_1_out14, demultiplexer_1_out15,
       demultiplexer_1_out16, demultiplexer_1_out17, demultiplexer_1_out18, demultiplexer_1_out19,
       demultiplexer_1_out20, demultiplexer_1_out21, demultiplexer_1_out22, demultiplexer_1_out23,
       demultiplexer_1_out24, demultiplexer_1_out25, demultiplexer_1_out26, demultiplexer_1_out27,
       demultiplexer_1_out28, demultiplexer_1_out29, demultiplexer_1_out30, demultiplexer_1_out31, undriven;
  wire [7:0] register_1_q, register_2_q, register_3_q, register_4_q, register_5_q, register_6_q,
       register_7_q, register_8_q, register_9_q, register_10_q, register_11_q, register_12_q, register_13_q,
       register_14_q, register_15_q, register_16_q, register_17_q, register_18_q, register_19_q,
       register_20_q, register_21_q, register_22_q, register_23_q, register_24_q, register_25_q,
       register_26_q, register_27_q, register_28_q, register_29_q, register_30_q, register_31_q,
       register_32_q;

  Demultiplexer #(.select(5)) demultiplexer_1 (
    .out0(demultiplexer_1_out0), .out1(demultiplexer_1_out1), .out2(demultiplexer_1_out2),
    .out3(demultiplexer_1_out3), .out4(demultiplexer_1_out4), .out5(demultiplexer_1_out5),
    .out6(demultiplexer_1_out6), .out7(demultiplexer_1_out7), .out8(demultiplexer_1_out8),
    .out9(demultiplexer_1_out9), .out10(demultiplexer_1_out10), .out11(demultiplexer_1_out11),
    .out12(demultiplexer_1_out12), .out13(demultiplexer_1_out13), .out14(demultiplexer_1_out14),
    .out15(demultiplexer_1_out15), .out16(demultiplexer_1_out16), .out17(demultiplexer_1_out17),
    .out18(demultiplexer_1_out18), .out19(demultiplexer_1_out19), .out20(demultiplexer_1_out20),
    .out21(demultiplexer_1_out21), .out22(demultiplexer_1_out22), .out23(demultiplexer_1_out23),
    .out24(demultiplexer_1_out24), .out25(demultiplexer_1_out25), .out26(demultiplexer_1_out26),
    .out27(demultiplexer_1_out27), .out28(demultiplexer_1_out28), .out29(demultiplexer_1_out29),
    .out30(demultiplexer_1_out30), .out31(demultiplexer_1_out31), .in(in_2), .sel(in_3));  // open: en
  Register register_1 (.D(in_1), .en(demultiplexer_1_out0), .Q(register_1_q), .clk(undriven));  // open: clr
  Register register_2 (.D(in_1), .en(demultiplexer_1_out4), .Q(register_2_q), .clk(undriven));  // open: clr
  Register register_3 (.D(in_1), .en(demultiplexer_1_out8), .Q(register_3_q), .clk(undriven));  // open: clr
  Register register_4 (.D(in_1), .en(demultiplexer_1_out12), .Q(register_4_q), .clk(undriven));  // open: clr
  Register register_5 (.D(in_1), .en(demultiplexer_1_out16), .Q(register_5_q), .clk(undriven));  // open: clr
  Register register_6 (.D(in_1), .en(demultiplexer_1_out20), .Q(register_6_q), .clk(undriven));  // open: clr
  Register register_7 (.D(in_1), .en(demultiplexer_1_out24), .Q(register_7_q), .clk(undriven));  // open: clr
  Register register_8 (.D(in_1), .en(demultiplexer_1_out28), .Q(register_8_q), .clk(undriven));  // open: clr
  Register register_9 (.D(in_1), .en(demultiplexer_1_out1), .Q(register_9_q), .clk(undriven));  // open: clr
  Register register_10 (.D(in_1), .en(demultiplexer_1_out5), .Q(register_10_q), .clk(undriven));  // open: clr
  Register register_11 (.D(in_1), .en(demultiplexer_1_out9), .Q(register_11_q), .clk(undriven));  // open: clr
  Register register_12 (.D(in_1), .en(demultiplexer_1_out13), .Q(register_12_q), .clk(undriven));  // open: clr
  Register register_13 (.D(in_1), .en(demultiplexer_1_out17), .Q(register_13_q), .clk(undriven));  // open: clr
  Register register_14 (.D(in_1), .en(demultiplexer_1_out21), .Q(register_14_q), .clk(undriven));  // open: clr
  Register register_15 (.D(in_1), .en(demultiplexer_1_out25), .Q(register_15_q), .clk(undriven));  // open: clr
  Register register_16 (.D(in_1), .en(demultiplexer_1_out29), .Q(register_16_q), .clk(undriven));  // open: clr
  Register register_17 (.D(in_1), .en(demultiplexer_1_out2), .Q(register_17_q), .clk(undriven));  // open: clr
  Register register_18 (.D(in_1), .en(demultiplexer_1_out6), .Q(register_18_q), .clk(undriven));  // open: clr
  Register register_19 (.D(in_1), .en(demultiplexer_1_out10), .Q(register_19_q), .clk(undriven));  // open: clr
  Register register_20 (.D(in_1), .en(demultiplexer_1_out14), .Q(register_20_q), .clk(undriven));  // open: clr
  Register register_21 (.D(in_1), .en(demultiplexer_1_out18), .Q(register_21_q), .clk(undriven));  // open: clr
  Register register_22 (.D(in_1), .en(demultiplexer_1_out22), .Q(register_22_q), .clk(undriven));  // open: clr
  Register register_23 (.D(in_1), .en(demultiplexer_1_out26), .Q(register_23_q), .clk(undriven));  // open: clr
  Register register_24 (.D(in_1), .en(demultiplexer_1_out30), .Q(register_24_q), .clk(undriven));  // open: clr
  Register register_25 (.D(in_1), .en(demultiplexer_1_out3), .Q(register_25_q), .clk(undriven));  // open: clr
  Register register_26 (.D(in_1), .en(demultiplexer_1_out7), .Q(register_26_q), .clk(undriven));  // open: clr
  Register register_27 (.D(in_1), .en(demultiplexer_1_out11), .Q(register_27_q), .clk(undriven));  // open: clr
  Register register_28 (.D(in_1), .en(demultiplexer_1_out15), .Q(register_28_q), .clk(undriven));  // open: clr
  Register register_29 (.D(in_1), .en(demultiplexer_1_out19), .Q(register_29_q), .clk(undriven));  // open: clr
  Register register_30 (.D(in_1), .en(demultiplexer_1_out23), .Q(register_30_q), .clk(undriven));  // open: clr
  Register register_31 (.D(in_1), .en(demultiplexer_1_out27), .Q(register_31_q), .clk(undriven));  // open: clr
  Register register_32 (.D(in_1), .en(demultiplexer_1_out31), .Q(register_32_q), .clk(undriven));  // open: clr
  Multiplexer #(.select(5), .width(8)) multiplexer_1 (
    .in0(register_1_q), .in1(register_9_q), .in2(register_17_q), .in3(register_25_q), .in4(register_2_q),
    .in5(register_10_q), .in6(register_18_q), .in7(register_26_q), .in8(register_3_q), .in9(register_11_q),
    .in10(register_19_q), .in11(register_27_q), .in12(register_4_q), .in13(register_12_q),
    .in14(register_20_q), .in15(register_28_q), .in16(register_5_q), .in17(register_13_q),
    .in18(register_21_q), .in19(register_29_q), .in20(register_6_q), .in21(register_14_q),
    .in22(register_22_q), .in23(register_30_q), .in24(register_7_q), .in25(register_15_q),
    .in26(register_23_q), .in27(register_31_q), .in28(register_8_q), .in29(register_16_q),
    .in30(register_24_q), .in31(register_32_q), .out(out_4), .sel(in_3));  // open: en
endmodule

module \_1024х8_ram__тестовая_версия  (
);

  wire undriven, undriven_3, undriven_5, undriven_7;
  wire [4:0] undriven_2, undriven_4, undriven_6, undriven_8;
  wire [7:0] demultiplexer_1_out0, demultiplexer_1_out1, demultiplexer_1_out2, demultiplexer_1_out3,
       demultiplexer_1_out4, demultiplexer_1_out5, demultiplexer_1_out6, demultiplexer_1_out7,
       demultiplexer_1_out8, demultiplexer_1_out9, demultiplexer_1_out10, demultiplexer_1_out11,
       demultiplexer_1_out12, demultiplexer_1_out13, demultiplexer_1_out14;

  Demultiplexer #(.select(5), .width(8)) demultiplexer_1 (
    .out0(demultiplexer_1_out0), .out1(demultiplexer_1_out1), .out2(demultiplexer_1_out2),
    .out3(demultiplexer_1_out3), .out4(demultiplexer_1_out4), .out5(demultiplexer_1_out5),
    .out6(demultiplexer_1_out6), .out7(demultiplexer_1_out7), .out8(demultiplexer_1_out8),
    .out9(demultiplexer_1_out9), .out10(demultiplexer_1_out10), .out11(demultiplexer_1_out11),
    .out12(demultiplexer_1_out12), .out13(demultiplexer_1_out13), .out14(demultiplexer_1_out14));  // open: out15, out16, out17, out18, out19, out20, out21, out22, out23, out24, out25, out26, out27, out28, out29, out30, out31, in, sel, en
  \_32_8ram__тестовая_версия  \u_32_8ram_тестовая_версия_1  (
    .in_1(demultiplexer_1_out0), .in_2(undriven), .in_3(undriven_2));  // open: out_4
  \_32_8ram__тестовая_версия  \u_32_8ram_тестовая_версия_2  (
    .in_1(demultiplexer_1_out4), .in_2(undriven), .in_3(undriven_2));  // open: out_4
  \_32_8ram__тестовая_версия  \u_32_8ram_тестовая_версия_3  (
    .in_1(demultiplexer_1_out8), .in_2(undriven), .in_3(undriven_2));  // open: out_4
  \_32_8ram__тестовая_версия  \u_32_8ram_тестовая_версия_4  (
    .in_1(demultiplexer_1_out12), .in_2(undriven), .in_3(undriven_2));  // open: out_4
  \_32_8ram__тестовая_версия  \u_32_8ram_тестовая_версия_5  (.in_2(undriven), .in_3(undriven_2));  // open: in_1, out_4
  \_32_8ram__тестовая_версия  \u_32_8ram_тестовая_версия_6  (.in_2(undriven), .in_3(undriven_2));  // open: in_1, out_4
  \_32_8ram__тестовая_версия  \u_32_8ram_тестовая_версия_7  (.in_2(undriven), .in_3(undriven_2));  // open: in_1, out_4
  \_32_8ram__тестовая_версия  \u_32_8ram_тестовая_версия_8  (
    .in_1(demultiplexer_1_out1), .in_2(undriven_3), .in_3(undriven_4));  // open: out_4
  \_32_8ram__тестовая_версия  \u_32_8ram_тестовая_версия_9  (
    .in_1(demultiplexer_1_out5), .in_2(undriven_3), .in_3(undriven_4));  // open: out_4
  \_32_8ram__тестовая_версия  \u_32_8ram_тестовая_версия_10  (
    .in_1(demultiplexer_1_out9), .in_2(undriven_3), .in_3(undriven_4));  // open: out_4
  \_32_8ram__тестовая_версия  \u_32_8ram_тестовая_версия_11  (
    .in_1(demultiplexer_1_out13), .in_2(undriven_3), .in_3(undriven_4));  // open: out_4
  \_32_8ram__тестовая_версия  \u_32_8ram_тестовая_версия_12  (
    .in_2(undriven_3), .in_3(undriven_4));  // open: in_1, out_4
  \_32_8ram__тестовая_версия  \u_32_8ram_тестовая_версия_13  (
    .in_2(undriven_3), .in_3(undriven_4));  // open: in_1, out_4
  \_32_8ram__тестовая_версия  \u_32_8ram_тестовая_версия_14  (
    .in_2(undriven_3), .in_3(undriven_4));  // open: in_1, out_4
  \_32_8ram__тестовая_версия  \u_32_8ram_тестовая_версия_15  (
    .in_1(demultiplexer_1_out2), .in_2(undriven_5), .in_3(undriven_6));  // open: out_4
  \_32_8ram__тестовая_версия  \u_32_8ram_тестовая_версия_16  (
    .in_1(demultiplexer_1_out6), .in_2(undriven_5), .in_3(undriven_6));  // open: out_4
  \_32_8ram__тестовая_версия  \u_32_8ram_тестовая_версия_17  (
    .in_1(demultiplexer_1_out10), .in_2(undriven_5), .in_3(undriven_6));  // open: out_4
  \_32_8ram__тестовая_версия  \u_32_8ram_тестовая_версия_18  (
    .in_1(demultiplexer_1_out14), .in_2(undriven_5), .in_3(undriven_6));  // open: out_4
  \_32_8ram__тестовая_версия  \u_32_8ram_тестовая_версия_19  (
    .in_2(undriven_5), .in_3(undriven_6));  // open: in_1, out_4
  \_32_8ram__тестовая_версия  \u_32_8ram_тестовая_версия_20  (
    .in_2(undriven_5), .in_3(undriven_6));  // open: in_1, out_4
  \_32_8ram__тестовая_версия  \u_32_8ram_тестовая_версия_21  (
    .in_2(undriven_5), .in_3(undriven_6));  // open: in_1, out_4
  \_32_8ram__тестовая_версия  \u_32_8ram_тестовая_версия_22  (
    .in_1(demultiplexer_1_out3), .in_2(undriven_7), .in_3(undriven_8));  // open: out_4
  \_32_8ram__тестовая_версия  \u_32_8ram_тестовая_версия_23  (
    .in_1(demultiplexer_1_out7), .in_2(undriven_7), .in_3(undriven_8));  // open: out_4
  \_32_8ram__тестовая_версия  \u_32_8ram_тестовая_версия_24  (
    .in_1(demultiplexer_1_out11), .in_2(undriven_7), .in_3(undriven_8));  // open: out_4
  \_32_8ram__тестовая_версия  \u_32_8ram_тестовая_версия_25  (
    .in_2(undriven_7), .in_3(undriven_8));  // open: in_1, out_4
  \_32_8ram__тестовая_версия  \u_32_8ram_тестовая_версия_26  (
    .in_2(undriven_7), .in_3(undriven_8));  // open: in_1, out_4
  \_32_8ram__тестовая_версия  \u_32_8ram_тестовая_версия_27  (
    .in_2(undriven_7), .in_3(undriven_8));  // open: in_1, out_4
  \_32_8ram__тестовая_версия  \u_32_8ram_тестовая_версия_28  (
    .in_2(undriven_7), .in_3(undriven_8));  // open: in_1, out_4
endmodule

module \_8х8ram  (
  input  [7:0] in_1,
  input  in_2,
  input  [2:0] in_3,
  output [7:0] out_4
);

  wire clock_1_out, demultiplexer_1_out0, demultiplexer_1_out1, demultiplexer_1_out2, demultiplexer_1_out3,
       demultiplexer_1_out4, demultiplexer_1_out5, demultiplexer_1_out6, demultiplexer_1_out7;
  wire [7:0] register_1_q, register_2_q, register_3_q, register_4_q, register_5_q, register_6_q,
       register_7_q, register_8_q;

  Demultiplexer #(.select(3)) demultiplexer_1 (
    .out0(demultiplexer_1_out0), .out1(demultiplexer_1_out1), .out2(demultiplexer_1_out2),
    .out3(demultiplexer_1_out3), .out4(demultiplexer_1_out4), .out5(demultiplexer_1_out5),
    .out6(demultiplexer_1_out6), .out7(demultiplexer_1_out7), .in(in_2), .sel(in_3));  // open: en
  Clock clock_1 (.out(clock_1_out));
  Register register_1 (.D(in_1), .en(demultiplexer_1_out0), .Q(register_1_q), .clk(clock_1_out));  // open: clr
  Register register_2 (.D(in_1), .en(demultiplexer_1_out1), .Q(register_2_q), .clk(clock_1_out));  // open: clr
  Register register_3 (.D(in_1), .en(demultiplexer_1_out2), .Q(register_3_q), .clk(clock_1_out));  // open: clr
  Register register_4 (.D(in_1), .en(demultiplexer_1_out3), .Q(register_4_q), .clk(clock_1_out));  // open: clr
  Register register_5 (.D(in_1), .en(demultiplexer_1_out4), .Q(register_5_q), .clk(clock_1_out));  // open: clr
  Register register_6 (.D(in_1), .en(demultiplexer_1_out5), .Q(register_6_q), .clk(clock_1_out));  // open: clr
  Register register_7 (.D(in_1), .en(demultiplexer_1_out6), .Q(register_7_q), .clk(clock_1_out));  // open: clr
  Register register_8 (.D(in_1), .en(demultiplexer_1_out7), .Q(register_8_q), .clk(clock_1_out));  // open: clr
  Multiplexer #(.select(3), .width(8)) multiplexer_1 (
    .in0(register_1_q), .in1(register_2_q), .in2(register_3_q), .in3(register_4_q), .in4(register_5_q),
    .in5(register_6_q), .in6(register_7_q), .in7(register_8_q), .out(out_4), .sel(in_3));  // open: en
endmodule

module _64x8ram (
  input  in_1,
  input  [2:0] in_2,
  input  [7:0] in_3,
  input  [2:0] in_4,
  output [7:0] out_5
);

  wire [7:0] demultiplexer_1_out0, demultiplexer_1_out1, demultiplexer_1_out2, demultiplexer_1_out3,
       demultiplexer_1_out4, demultiplexer_1_out5, demultiplexer_1_out6, demultiplexer_1_out7,
       \n8х8ram_1_out_4 , \n8х8ram_2_out_4 , \n8х8ram_3_out_4 , \n8х8ram_4_out_4 , \n8х8ram_5_out_4 ,
       \n8х8ram_6_out_4 , \n8х8ram_7_out_4 , \n8х8ram_8_out_4 ;

  Demultiplexer #(.select(3), .width(8)) demultiplexer_1 (
    .out0(demultiplexer_1_out0), .out1(demultiplexer_1_out1), .out2(demultiplexer_1_out2),
    .out3(demultiplexer_1_out3), .out4(demultiplexer_1_out4), .out5(demultiplexer_1_out5),
    .out6(demultiplexer_1_out6), .out7(demultiplexer_1_out7), .in(in_3), .sel(in_4));  // open: en
  \_8х8ram  \u_8х8ram_1  (.in_1(demultiplexer_1_out0), .in_2(in_1), .in_3(in_2), .out_4(\n8х8ram_1_out_4 ));
  \_8х8ram  \u_8х8ram_2  (.in_1(demultiplexer_1_out2), .in_2(in_1), .in_3(in_2), .out_4(\n8х8ram_2_out_4 ));
  \_8х8ram  \u_8х8ram_3  (.in_1(demultiplexer_1_out4), .in_2(in_1), .in_3(in_2), .out_4(\n8х8ram_3_out_4 ));
  \_8х8ram  \u_8х8ram_4  (.in_1(demultiplexer_1_out6), .in_2(in_1), .in_3(in_2), .out_4(\n8х8ram_4_out_4 ));
  \_8х8ram  \u_8х8ram_5  (.in_1(demultiplexer_1_out1), .in_2(in_1), .in_3(in_2), .out_4(\n8х8ram_5_out_4 ));
  \_8х8ram  \u_8х8ram_6  (.in_1(demultiplexer_1_out3), .in_2(in_1), .in_3(in_2), .out_4(\n8х8ram_6_out_4 ));
  \_8х8ram  \u_8х8ram_7  (.in_1(demultiplexer_1_out5), .in_2(in_1), .in_3(in_2), .out_4(\n8х8ram_7_out_4 ));
  \_8х8ram  \u_8х8ram_8  (.in_1(demultiplexer_1_out7), .in_2(in_1), .in_3(in_2), .out_4(\n8х8ram_8_out_4 ));
  Multiplexer #(.select(3), .width(8)) multiplexer_1 (
    .in0(\n8х8ram_1_out_4 ), .in1(\n8х8ram_5_out_4 ), .in2(\n8х8ram_2_out_4 ), .in3(\n8х8ram_6_out_4 ),
    .in4(\n8х8ram_3_out_4 ), .in5(\n8х8ram_7_out_4 ), .in6(\n8х8ram_4_out_4 ), .in7(\n8х8ram_8_out_4 ),
    .out(out_5), .sel(in_4));  // open: en
endmodule

module \_256х8ram  (
  input  [2:0] in_1,
  input  [2:0] in_2,
  input  in_3,
  input  [7:0] in_4,
  input  [1:0] in_5,
  output [7:0] out_6
);

  wire [7:0] demultiplexer_1_out0, demultiplexer_1_out1, demultiplexer_1_out2, demultiplexer_1_out3,
       n64x8ram_1_out_5, n64x8ram_2_out_5, n64x8ram_3_out_5, n64x8ram_4_out_5;

  Demultiplexer #(.select(2), .width(8)) demultiplexer_1 (
    .out0(demultiplexer_1_out0), .out1(demultiplexer_1_out1), .out2(demultiplexer_1_out2),
    .out3(demultiplexer_1_out3), .in(in_4), .sel(in_5));  // open: en
  _64x8ram u_64x8ram_1 (.in_3(demultiplexer_1_out0), .out_5(n64x8ram_1_out_5), .in_1(in_3), .in_4(in_1), .in_2(in_2));
  _64x8ram u_64x8ram_2 (.in_3(demultiplexer_1_out1), .out_5(n64x8ram_2_out_5), .in_1(in_3), .in_4(in_1), .in_2(in_2));
  _64x8ram u_64x8ram_3 (.in_3(demultiplexer_1_out2), .out_5(n64x8ram_3_out_5), .in_1(in_3), .in_4(in_1), .in_2(in_2));
  _64x8ram u_64x8ram_4 (.in_3(demultiplexer_1_out3), .out_5(n64x8ram_4_out_5), .in_1(in_3), .in_4(in_1), .in_2(in_2));
  Multiplexer #(.select(2), .width(8)) multiplexer_1 (
    .in0(n64x8ram_1_out_5), .in1(n64x8ram_2_out_5), .in2(n64x8ram_3_out_5), .in3(n64x8ram_4_out_5),
    .out(out_6), .sel(in_5));  // open: en
endmodule

module \_1024х8ram  (
  input  in_1,
  input  [2:0] in_2,
  input  [2:0] in_3,
  input  [1:0] in_4,
  input  [7:0] in_5,
  input  [1:0] in_6,
  output [7:0] out_7
);

  wire [7:0] demultiplexer_1_out0, demultiplexer_1_out1, demultiplexer_1_out2, demultiplexer_1_out3,
       \n256х8ram_1_out_6 , \n256х8ram_2_out_6 , \n256х8ram_3_out_6 , \n256х8ram_4_out_6 ;

  Demultiplexer #(.select(2), .width(8)) demultiplexer_1 (
    .out0(demultiplexer_1_out0), .out1(demultiplexer_1_out1), .out2(demultiplexer_1_out2),
    .out3(demultiplexer_1_out3), .in(in_5), .sel(in_6));  // open: en
  \_256х8ram  \u_256х8ram_1  (
    .in_1(in_3), .in_2(in_2), .in_3(in_1), .in_4(demultiplexer_1_out0), .in_5(in_4),
    .out_6(\n256х8ram_1_out_6 ));
  \_256х8ram  \u_256х8ram_2  (
    .in_1(in_3), .in_2(in_2), .in_3(in_1), .in_4(demultiplexer_1_out1), .in_5(in_4),
    .out_6(\n256х8ram_2_out_6 ));
  \_256х8ram  \u_256х8ram_3  (
    .in_1(in_3), .in_2(in_2), .in_3(in_1), .in_4(demultiplexer_1_out2), .in_5(in_4),
    .out_6(\n256х8ram_3_out_6 ));
  \_256х8ram  \u_256х8ram_4  (
    .in_1(in_3), .in_2(in_2), .in_3(in_1), .in_4(demultiplexer_1_out3), .in_5(in_4),
    .out_6(\n256х8ram_4_out_6 ));
  Multiplexer #(.select(2), .width(8)) multiplexer_1 (
    .in0(\n256х8ram_1_out_6 ), .in1(\n256х8ram_2_out_6 ), .in2(\n256х8ram_3_out_6 ),
    .in3(\n256х8ram_4_out_6 ), .out(out_7), .sel(in_6));  // open: en
endmodule
